# Fritzing sketch Circuit (saved by Fritzing 0.9.3b)
breadboards: 1

parts:
  Tiva_C_LaunchPad1 = Tiva C TM4C123G [package=THT]
  S5 = Toggle Switch spst [package=THT]
  S6 = Momentary Switch 6mm 2pin
  S7 = Momentary Switch 6mm 2pin
  S8 = Momentary Switch 6mm 2pin
  S9 = Momentary Switch 6mm 2pin
  JL012-13-5_1 = JL012-13-5.2 Lever (Limit) Switch SPDT + NO + NC [part_number=JL012-13-5.2]
  JL012-13-5_2 = JL012-13-5.2 Lever (Limit) Switch SPDT + NO + NC [part_number=JL012-13-5.2]
  M1 = fc-51 [package=THT]
  L298N1 = L298N DC motor driver
  M2 = DC Motor
  VCC1 = Battery block 9V
  R1 = Resistor [tolerance=±5% resistance=220 package=THT]
  R2 = Resistor [tolerance=±5% resistance=220 package=THT]
  R3 = Resistor [tolerance=±5% resistance=220 package=THT]
  R4 = Resistor [tolerance=±5% resistance=220 package=THT]
  C1 = Ceramic Capacitor [capacitance=100nF package="100 mil [THT, multilayer]"]
  C2 = Ceramic Capacitor [capacitance=100nF package="100 mil [THT, multilayer]"]
  C3 = Ceramic Capacitor [capacitance=100nF package="100 mil [THT, multilayer]"]
  C4 = Ceramic Capacitor [capacitance=100nF package="100 mil [THT, multilayer]"]
  R5 = Resistor [tolerance=±5% resistance=220 package=THT]

nets:
  N1: Tiva_C_LaunchPad1.PA5, S9.2, R4.Pin_0, C3.0
  N2: Tiva_C_LaunchPad1.PA6, L298N1.IN1
  N3: Tiva_C_LaunchPad1.PA7, L298N1.IN2
  N4: Tiva_C_LaunchPad1.5V, S5.COM, S6.1, S7.1, S8.1, S9.1, M1.pin3
  GND: Tiva_C_LaunchPad1.GND, JL012-13-5_1.C, JL012-13-5_2.C, M1.pin2, L298N1.GND, VCC1.-, R1.Pin_1, R2.Pin_0, R3.Pin_0, R4.Pin_1, C1.1, C2.1, C3.1, C4.1, R5.Pin_0
  N5: Tiva_C_LaunchPad1.PD6, S8.2, R3.Pin_1, C2.0
  N6: Tiva_C_LaunchPad1.PD7, S6.2, R1.Pin_0, C4.0
  N7: Tiva_C_LaunchPad1.PF3, S7.2, R2.Pin_1, C1.0
  N8: Tiva_C_LaunchPad1.PF0, M1.pin1
  N9: Tiva_C_LaunchPad1.RST, JL012-13-5_1.NO
  N10: Tiva_C_LaunchPad1.PB7, JL012-13-5_2.NO
  N11: Tiva_C_LaunchPad1.PB6, S5.L1, R5.Pin_1
  N12: L298N1.OUT1, M2.pin_2
  N13: L298N1.OUT2, M2.pin_1
  N14: L298N1.12V, VCC1.+
  N15: L298N1.5V, L298N1.ENA

custom parts:
  Tiva C TM4C123G: Tiva C LaunchPad EK-TM4C123GXL
  Toggle Switch spst: Toggle Switch single pole single throw
  Momentary Switch 6mm 2pin: Momentary Switch 6mm 2 pin Button commonly used for reset or general input.
  JL012-13-5.2 Lever (Limit) Switch SPDT + NO + NC: Micro Switch; Model No.: JL012-13.5-2; Actuator Action: Momentary; Actuator Type: Hinge Lever; Contact Configuration: 1NO, 1NC (SPDT) Temperature -25~65℃；Relative humidity: below 85%; Rate Voltage: 125V AC; Rated Current: 1A.
  L298N DC motor driver: 2x DC motor driver with 78M05 positive voltage regulator (7..35 V) L298N: max 46 V, 2 A Set 5 V Enable jumper to enable 5 V regultor (needed for the L298N) and +5 V output at screw terminal or supply external +5 V at screw terminal Set ENA and/or ENB to +5 V to enable motor permanently or supply ENA and/or ENB with PWM signal IN1 and IN2 set rotation directory for motor A (OUT1/OUT2) IN2 and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
